# Fritzing sketch strip_game (saved by Fritzing 0.9.4)
breadboards: 1

parts:
  WeMos_D1_Mini1 = WeMos D1 Mini  # not connected
  Part1 = ws2812b [package="smd 2812b"]  # not connected
  Part2 = ws2812b [package="smd 2812b"]  # not connected
  S1 = Pushbutton [package="[SMD]"]
  J1 = Piezo Speaker

nets:
  N1: S1.Pin_1, S1.Pin_2, J1.pin1
  N2: S1.Pin_3, S1.Pin_4
